# Fritzing sketch lab3 (saved by Fritzing 0.9.3b)
breadboards: 1

parts:
  41MUX_for_routing = IC, DIP package, 16 pins [chip_label=153]  # not connected
  21MUX = IC, DIP package, 16 pins [chip_label=157]  # not connected
  NAND = IC, DIP package, 14 pins [chip_label=00]  # not connected
  NOR = IC, DIP package, 14 pins [chip_label=02]  # not connected
  XOR = IC, DIP package, 14 pins [chip_label=86]  # not connected
  NOT = IC, DIP package, 14 pins [chip_label=04]  # not connected
  SR-B = IC, DIP package, 16 pins [chip_label="194 SR"]
  SR-A = IC, DIP package, 16 pins [chip_label="194 SR"]
  41MUX_for_computation = IC, DIP package, 16 pins [chip_label=153]  # not connected

nets:
  5V: SR-B.pin1, SR-A.pin1
  D3: SR-B.pin3, SR-A.pin3
  D2: SR-B.pin4, SR-A.pin4
  D1: SR-B.pin5, SR-A.pin5
  D0: SR-B.pin6, SR-A.pin6
  CLK: SR-B.pin11, SR-A.pin11
  SR-B: SR-B.pin12
  SR-A: SR-A.pin12
